// Logisim project imm-gen.circ as structural Verilog: 1 circuit, main circuit imm_gen
module imm_gen (
  input  [31:0] Instruction,
  input  [2:0] ImmSel,
  output [31:0] Immediate
);

  wire [19:0] bit_extender_2_out;
  wire [20:0] bit_extender_1_out;
  wire [31:0] bit_extender_3_out;

  assign bit_extender_1_out = {{20{Instruction[31]}}, Instruction[31]};  // Bit_Extender bit_extender_1
  assign bit_extender_2_out = {{19{Instruction[31]}}, Instruction[31]};  // Bit_Extender bit_extender_2
  assign bit_extender_3_out = {{20{Instruction[31]}}, Instruction[31:20]};  // Bit_Extender bit_extender_3
  Multiplexer #(.select(3), .width(32)) multiplexer_1 (
    .in0(bit_extender_3_out), .in1({bit_extender_1_out, Instruction[30:25], Instruction[11:7]}),
    .in2({bit_extender_2_out, Instruction[7], Instruction[30:25], Instruction[11:8], 1'b0}), .out(Immediate),
    .sel(ImmSel));  // open: in3, in4, in5, in6, in7

  // Notes on the sheet:
  //   INPUTS to your circuit
  //   DON'T CHANGE THE LOCATIONS OF THE INPUTS AND OUTPUTS!
  //   OUTPUT from your circuit
endmodule
