// Logisim project partial-load.circ as structural Verilog: 1 circuit, main circuit partial_load
module partial_load (
  input  [31:0] Instruction,
  input  [31:0] MemAddress,
  input  [31:0] DataFromMem,
  output [31:0] DataToReg
);

  wire bottom2bit_00, bottom2bit_01, bottom2bit_10, bottom2bit_11, is_lb, is_lh, is_lw;
  wire [1:0] bottom2bitsIndex, loadIndex;
  wire [7:0] multiplexer_1_out;
  wire [15:0] multiplexer_2_out;
  wire [31:0] lbOutput, lhOutput;

  Comparator #(.width(2)) comparator_1 (.a(2'b00), .b(MemAddress[1:0]), .eq(bottom2bit_00));  // open: gt, lt
  Comparator #(.width(2)) comparator_2 (.a(2'b01), .b(MemAddress[1:0]), .eq(bottom2bit_01));  // open: gt, lt
  Comparator #(.width(2)) comparator_3 (.a(2'b10), .b(MemAddress[1:0]), .eq(bottom2bit_10));  // open: gt, lt
  Comparator #(.width(2)) comparator_4 (.a(2'b11), .b(MemAddress[1:0]), .eq(bottom2bit_11));  // open: gt, lt
  Demultiplexer #(.select(3)) demultiplexer_1 (
    .out0(is_lb), .out1(is_lh), .out2(is_lw), .in(1'b1), .sel(Instruction[14:12]));  // open: out3, out4, out5, out6, out7
  Priority_Encoder #(.select_enc(2)) priority_encoder_1 (
    .in0(bottom2bit_00), .in1(bottom2bit_01), .in2(bottom2bit_10), .in3(bottom2bit_11), .out(bottom2bitsIndex));  // open: gs, en_out, en_in
  Multiplexer #(.select(2), .width(8)) multiplexer_1 (
    .in0(DataFromMem[7:0]), .in1(DataFromMem[15:8]), .in2(DataFromMem[23:16]), .in3(DataFromMem[31:24]),
    .out(multiplexer_1_out), .sel(bottom2bitsIndex));
  Multiplexer #(.select(2), .width(16)) multiplexer_2 (
    .in0(DataFromMem[15:0]), .in1(DataFromMem[23:8]), .in2(DataFromMem[31:16]), .out(multiplexer_2_out),
    .sel(bottom2bitsIndex));  // open: in3
  assign lbOutput = {{24{multiplexer_1_out[7]}}, multiplexer_1_out};  // Bit_Extender bit_extender_1
  assign lhOutput = {{16{multiplexer_2_out[15]}}, multiplexer_2_out};  // Bit_Extender bit_extender_2
  Priority_Encoder #(.select_enc(2)) priority_encoder_2 (
    .in0(is_lb), .in1(is_lh), .in2(is_lw), .out(loadIndex));  // open: in3, gs, en_out, en_in
  Multiplexer #(.select(2), .width(32)) multiplexer_3 (
    .in0(lbOutput), .in1(lhOutput), .in2(DataFromMem), .out(DataToReg), .sel(loadIndex));  // open: in3

  // Other names for the same wires on the sheet: lwOutput[31:0] = DataFromMem; bottom2bits[1:0] = MemAddress[1:0]

  // Notes on the sheet:
  //   INPUTS to your circuit
  //   DON'T CHANGE THE LOCATIONS OF THE INPUTS AND OUTPUTS!
  //   OUTPUT from your circuit
endmodule
