// Logisim project regfile.circ as structural Verilog: 1 circuit, main circuit regfile
module regfile (
  input  [4:0] ReadReg1,
  input  [4:0] ReadReg2,
  input  [4:0] WriteReg,
  input  [31:0] RegWriteData,
  input  RegWEn,
  input  clk,
  output [31:0] ra,
  output [31:0] sp,
  output [31:0] t0,
  output [31:0] t1,
  output [31:0] t2,
  output [31:0] s0,
  output [31:0] s1,
  output [31:0] a0,
  output [31:0] RegReadData1,
  output [31:0] RegReadData2
);

  wire x0WE, x1WE, x2WE, x3WE, x4WE, x5WE, x6WE, x7WE, x8WE, x9WE, x10WE, x11WE, x12WE, x13WE, x14WE, x15WE,
       x16WE, x17WE, x18WE, x19WE, x20WE, x21WE, x22WE, x23WE, x24WE, x25WE, x26WE, x27WE, x28WE, x29WE,
       x30WE, x31WE;
  wire [31:0] a1, a2, a3, a4, a5, a6, a7, gp, s2, s3, s4, s5, s6, s7, s8, s9, s10, s11, t3, t4, t5, t6, tp,
       zero;

  Register #(.width(32)) x6 (.D(RegWriteData), .en(x6WE), .clk(clk), .Q(t1));  // open: clr
  Register #(.width(32)) x7 (.D(RegWriteData), .en(x7WE), .clk(clk), .Q(t2));  // open: clr
  Demultiplexer #(.select(5)) demultiplexer_1 (
    .out0(x0WE), .out1(x1WE), .out2(x2WE), .out3(x3WE), .out4(x4WE), .out5(x5WE), .out6(x6WE), .out7(x7WE),
    .out8(x8WE), .out9(x9WE), .out10(x10WE), .out11(x11WE), .out12(x12WE), .out13(x13WE), .out14(x14WE),
    .out15(x15WE), .out16(x16WE), .out17(x17WE), .out18(x18WE), .out19(x19WE), .out20(x20WE), .out21(x21WE),
    .out22(x22WE), .out23(x23WE), .out24(x24WE), .out25(x25WE), .out26(x26WE), .out27(x27WE), .out28(x28WE),
    .out29(x29WE), .out30(x30WE), .out31(x31WE), .in(RegWEn), .sel(WriteReg));
  Register #(.width(32)) x0 (.D({32{1'b0}}), .en(1'b0), .clk(clk), .Q(zero));  // open: clr
  Register #(.width(32)) x3 (.D(RegWriteData), .en(x3WE), .clk(clk), .Q(gp));  // open: clr
  Register #(.width(32)) x8 (.D(RegWriteData), .en(x8WE), .clk(clk), .Q(s0));  // open: clr
  Register #(.width(32)) x1 (.D(RegWriteData), .en(x1WE), .clk(clk), .Q(ra));  // open: clr
  Register #(.width(32)) x4 (.D(RegWriteData), .en(x4WE), .clk(clk), .Q(tp));  // open: clr
  Register #(.width(32)) x2 (.D(RegWriteData), .en(x2WE), .clk(clk), .Q(sp));  // open: clr
  Register #(.width(32)) x9 (.D(RegWriteData), .en(x9WE), .clk(clk), .Q(s1));  // open: clr
  Register #(.width(32)) x5 (.D(RegWriteData), .en(x5WE), .clk(clk), .Q(t0));  // open: clr
  Register #(.width(32)) x10 (.D(RegWriteData), .en(x10WE), .clk(clk), .Q(a0));  // open: clr
  Register #(.width(32)) x11 (.D(RegWriteData), .en(x11WE), .clk(clk), .Q(a1));  // open: clr
  Multiplexer #(.select(5), .width(32)) multiplexer_1 (
    .in0(zero), .in1(ra), .in2(sp), .in3(gp), .in4(tp), .in5(t0), .in6(t1), .in7(t2), .in8(s0), .in9(s1),
    .in10(a0), .in11(a1), .in12(a2), .in13(a3), .in14(a4), .in15(a5), .in16(a6), .in17(a7), .in18(s2),
    .in19(s3), .in20(s4), .in21(s5), .in22(s6), .in23(s7), .in24(s8), .in25(s9), .in26(s10), .in27(s11),
    .in28(t3), .in29(t4), .in30(t5), .in31(t6), .out(RegReadData1), .sel(ReadReg1));
  Register #(.width(32)) x12 (.D(RegWriteData), .en(x12WE), .clk(clk), .Q(a2));  // open: clr
  Register #(.width(32)) x14 (.D(RegWriteData), .en(x14WE), .clk(clk), .Q(a4));  // open: clr
  Register #(.width(32)) x16 (.D(RegWriteData), .en(x16WE), .clk(clk), .Q(a6));  // open: clr
  Register #(.width(32)) x13 (.D(RegWriteData), .en(x13WE), .clk(clk), .Q(a3));  // open: clr
  Register #(.width(32)) x15 (.D(RegWriteData), .en(x15WE), .clk(clk), .Q(a5));  // open: clr
  Register #(.width(32)) x17 (.D(RegWriteData), .en(x17WE), .clk(clk), .Q(a7));  // open: clr
  Register #(.width(32)) x18 (.D(RegWriteData), .en(x18WE), .clk(clk), .Q(s2));  // open: clr
  Register #(.width(32)) x19 (.D(RegWriteData), .en(x19WE), .clk(clk), .Q(s3));  // open: clr
  Register #(.width(32)) x20 (.D(RegWriteData), .en(x20WE), .clk(clk), .Q(s4));  // open: clr
  Register #(.width(32)) x21 (.D(RegWriteData), .en(x21WE), .clk(clk), .Q(s5));  // open: clr
  Register #(.width(32)) x22 (.D(RegWriteData), .en(x22WE), .clk(clk), .Q(s6));  // open: clr
  Register #(.width(32)) x23 (.D(RegWriteData), .en(x23WE), .clk(clk), .Q(s7));  // open: clr
  Register #(.width(32)) x24 (.D(RegWriteData), .en(x24WE), .clk(clk), .Q(s8));  // open: clr
  Register #(.width(32)) x25 (.D(RegWriteData), .en(x25WE), .clk(clk), .Q(s9));  // open: clr
  Register #(.width(32)) x27 (.D(RegWriteData), .en(x27WE), .clk(clk), .Q(s11));  // open: clr
  Register #(.width(32)) x28 (.D(RegWriteData), .en(x28WE), .clk(clk), .Q(t3));  // open: clr
  Register #(.width(32)) x26 (.D(RegWriteData), .en(x26WE), .clk(clk), .Q(s10));  // open: clr
  Register #(.width(32)) x30 (.D(RegWriteData), .en(x30WE), .clk(clk), .Q(t5));  // open: clr
  Register #(.width(32)) x31 (.D(RegWriteData), .en(x31WE), .clk(clk), .Q(t6));  // open: clr
  Multiplexer #(.select(5), .width(32)) multiplexer_2 (
    .in0(zero), .in1(ra), .in2(sp), .in3(gp), .in4(tp), .in5(t0), .in6(t1), .in7(t2), .in8(s0), .in9(s1),
    .in10(a0), .in11(a1), .in12(a2), .in13(a3), .in14(a4), .in15(a5), .in16(a6), .in17(a7), .in18(s2),
    .in19(s3), .in20(s4), .in21(s5), .in22(s6), .in23(s7), .in24(s8), .in25(s9), .in26(s10), .in27(s11),
    .in28(t3), .in29(t4), .in30(t5), .in31(t6), .out(RegReadData2), .sel(ReadReg2));
  Register #(.width(32)) x29 (.D(RegWriteData), .en(x29WE), .clk(clk), .Q(t4));  // open: clr

  // Notes on the sheet:
  //   INPUTS to your circuit
  //   DON'T CHANGE THE LOCATIONS OF THE INPUTS AND OUTPUTS!
  //   These are DEBUG/TEST outputs from your circuit.
  //   OUTPUTS from your circuit
endmodule
